# Fritzing sketch angler_fish_circuit (saved by Fritzing 0.9.2b)
breadboards: 1

parts:
  S1 = Pushbutton [package="[THT]"]
  RGB_SMD_LED1 = SMD RGB LED (WS2812) [package=5050]
  BAT1 = Battery Holders [package=battcom_20mm_pth]
  U1 = attiny85 [package=dip]

nets:
  N1: S1.Pin_1, S1.Pin_2, RGB_SMD_LED1.VSS, BAT1.+, U1.Pin_4
  N2: S1.Pin_3, S1.Pin_4, U1.Pin_2
  N3: RGB_SMD_LED1.DIn, U1.Pin_7
  N4: RGB_SMD_LED1.VCC, BAT1.-, U1.Pin_8
